# Fritzing sketch kuka_arduino_basic (saved by Fritzing 0.9.1b)
breadboards: 1

parts:
  U1 = Optocoupler [package=THT]
  R1 = Resistor [tolerance=±5% resistance=1k package=THT]
  R3 = Resistor [tolerance=±20% resistance=10k package=THT]
  Part1 = Arduino Uno (Rev3) - ICSP
  U2 = Optocoupler [package=THT]
  R4 = Resistor [tolerance=±5% resistance=1k package=THT]
  R5 = Resistor [tolerance=±20% resistance=10k package=THT]
  U3 = Optocoupler [package=THT]
  R6 = Resistor [tolerance=±5% resistance=1k package=THT]
  R7 = Resistor [tolerance=±20% resistance=220 package=THT]
  U4 = Optocoupler [package=THT]
  R8 = Resistor [tolerance=±5% resistance=1k package=THT]
  R9 = Resistor [tolerance=±20% resistance=220 package=THT]

nets:
  N1: U1.Pin_1, R1.Pin_0
  N2: U1.Pin_2, U2.Pin_2, R6.Pin_0, R8.Pin_0
  N3: U1.Pin_4, R3.Pin_1, Part1.D2
  N4: U1.Pin_5, Part1.5V, U2.Pin_5
  N5: R3.Pin_0, Part1.GND, R5.Pin_0, U3.Pin_2, U4.Pin_2
  N6: Part1.D3_PWM, U2.Pin_4, R5.Pin_1
  N7: Part1.D4, R9.Pin_1
  N8: Part1.D5_PWM, R7.Pin_1
  N9: U2.Pin_1, R4.Pin_0
  N10: U3.Pin_1, R7.Pin_0
  N11: U3.Pin_4, R6.Pin_1
  N12: U3.Pin_5, U4.Pin_5
  N13: U4.Pin_1, R9.Pin_0
  N14: U4.Pin_4, R8.Pin_1

notes:
  PURPLE to KUKA INPUT-2 24V
  ORANGE to KUKA INPUT-1 24V
  GREEN to KUKA OUTPUT-2 24V
  YELLOW to KUKA OUTPUT-1 24V
  RED to KUKA +24V
  BLACK to KUKA GND (-)
